# Fritzing sketch LedMatrix (saved by Fritzing 0.7.10b)
breadboards: 1

parts:
  LED00 = LED - 5mm [color="Red (633nm)" package="5 mm [THT]"]
  LED01 = LED - 5mm [color="Red (633nm)" package="5 mm [THT]"]
  LED02 = LED - 5mm [color="Red (633nm)" package="5 mm [THT]"]
  LED03 = LED - 5mm [color="Red (633nm)" package="5 mm [THT]"]
  LED04 = LED - 5mm [color="Red (633nm)" package="5 mm [THT]"]
  LED14 = LED - 5mm [color="Red (633nm)" package="5 mm [THT]"]
  LED13 = LED - 5mm [color="Red (633nm)" package="5 mm [THT]"]
  LED11 = LED - 5mm [color="Red (633nm)" package="5 mm [THT]"]
  LED10 = LED - 5mm [color="Red (633nm)" package="5 mm [THT]"]
  LED12 = LED - 5mm [color="Red (633nm)" package="5 mm [THT]"]
  LED24 = LED - 5mm [color="Red (633nm)" package="5 mm [THT]"]
  LED23 = LED - 5mm [color="Red (633nm)" package="5 mm [THT]"]
  LED21 = LED - 5mm [color="Red (633nm)" package="5 mm [THT]"]
  LED20 = LED - 5mm [color="Red (633nm)" package="5 mm [THT]"]
  LED22 = LED - 5mm [color="Red (633nm)" package="5 mm [THT]"]
  LED34 = LED - 5mm [color="Red (633nm)" package="5 mm [THT]"]
  LED33 = LED - 5mm [color="Red (633nm)" package="5 mm [THT]"]
  LED31 = LED - 5mm [color="Red (633nm)" package="5 mm [THT]"]
  LED30 = LED - 5mm [color="Red (633nm)" package="5 mm [THT]"]
  LED32 = LED - 5mm [color="Red (633nm)" package="5 mm [THT]"]
  LED44 = LED - 5mm [color="Red (633nm)" package="5 mm [THT]"]
  LED43 = LED - 5mm [color="Red (633nm)" package="5 mm [THT]"]
  LED41 = LED - 5mm [color="Red (633nm)" package="5 mm [THT]"]
  LED40 = LED - 5mm [color="Red (633nm)" package="5 mm [THT]"]
  LED42 = LED - 5mm [color="Red (633nm)" package="5 mm [THT]"]
  R1 = Resistor [tolerance=±5% resistance=220 package=THT]
  R2 = Resistor [tolerance=±5% resistance=220 package=THT]
  R3 = Resistor [tolerance=±5% resistance=220 package=THT]
  R4 = Resistor [tolerance=±5% resistance=220 package=THT]
  R5 = Resistor [tolerance=±5% resistance=220 package=THT]
  Arduino1 = Arduino

nets:
  N1: LED00.cathode, LED01.cathode, LED02.cathode, LED03.cathode, LED04.cathode, Arduino1.D5
  N2: LED00.anode, LED10.anode, LED20.anode, LED30.anode, LED40.anode, R1.Pin_0
  N3: LED01.anode, LED11.anode, LED21.anode, LED31.anode, LED41.anode, R2.Pin_0
  N4: LED02.anode, LED12.anode, LED22.anode, LED32.anode, LED42.anode, R3.Pin_0
  N5: LED03.anode, LED13.anode, LED23.anode, LED33.anode, LED43.anode, R4.Pin_0
  N6: LED04.anode, LED14.anode, LED24.anode, LED34.anode, LED44.anode, R5.Pin_0
  N7: LED14.cathode, LED13.cathode, LED11.cathode, LED10.cathode, LED12.cathode, Arduino1.D6
  N8: LED24.cathode, LED23.cathode, LED21.cathode, LED20.cathode, LED22.cathode, Arduino1.D9
  N9: LED34.cathode, LED33.cathode, LED31.cathode, LED30.cathode, LED32.cathode, Arduino1.D10
  N10: LED44.cathode, LED43.cathode, LED41.cathode, LED40.cathode, LED42.cathode, Arduino1.D11
  N11: R1.Pin_1, Arduino1.D13
  N12: R2.Pin_1, Arduino1.D12
  N13: R3.Pin_1, Arduino1.D8
  N14: R4.Pin_1, Arduino1.D7
  N15: R5.Pin_1, Arduino1.D4
